# Fritzing sketch ardBeeQueenFritz (saved by Fritzing 0.9.2b)
breadboards: 1

parts:
  Part1 = Arduino Pro Mini v13
  Part2 = KY-019 5V Relay Module [package="Breakout board"]
  R1 = Resistor [tolerance=±5% resistance=4.7k package=THT]
  X1 = USB Connectors [package=usb-microb]
  DS1 = DS18B20 1-Wire Temperature Sensor [part_number=DS18B20]

nets:
  N1: Part1.RAW, X1.VBUS
  GND: Part1.GND, Part2.-, X1.GND, DS1.GND
  VCC: Part1.VCC, Part2.+, R1.Pin_0, DS1.VDD
  N2: Part1.D3_PWM, Part2.S
  N3: Part1.D2, R1.Pin_1, DS1.DQ

custom parts:
  KY-019 5V Relay Module: KY-019 5V Relay module, used to control AC circuits.
